# Fritzing sketch Protoboard (saved by Fritzing 0.9.3b)
breadboards: 4

parts:
  M1 = DOIT Esp32 DevKit v1 (30 pins long, 11 pins width) [part_number=ESP32S-PIN30]
  LCD1 = TFT 1.8 inch 160x128 w SD
  SIM800L_BO1 = SIM800L BO
  T1 = LM35 Temperature Sensor [package="TO92 [THT]"]
  U1 = LM2596 step down module
  U2 = Voltage Regulator - 5V [package="DPak [SMD]"]
  C1 = Capacitor Polarized [package=cpol-radial-10uf-25v]
  RFID = RFID-RC522-v2
  M2 = TP4056 Module [part_number=HW-107]
  U3 = MPC1700 [package=sot23-3]
  C2 = Ceramic Capacitor [capacitance=100nF package="100 mil [THT, multilayer]"]
  C3 = Capacitor Polarized [package=cpol-radial-100uf-25v]
  Relay_BC548_12 = Keyes Relay [package=THT]
  Relay_BC548_32 = Keyes Relay [package=THT]
  Solar_Panel = Solar Cell
  BAT1 = Battery Holders [package=lipo-1100mAh]
  GY1 = MPU-6050 Board GY-521 [form="♀ (female)" package=THT]
  M3 = BME280

nets:
  3V3: M1.3V3, LCD1.pin_1, RFID.3.3V, U3.OUT, C2.0, C3.+, GY1.pin1, M3.VIN
  GND: M1.GND, LCD1.pin2, SIM800L_BO1.pin_6, T1.GND, U1.IN-, U1.OUT-, U2.GND, U2.output_voltage, C1.-, RFID.GND, M2.pin2, U3.GND, C2.1, C3.-, GY1.pin2, M3.GND
  N1: M1.D15, GY1.pin3, M3.SCL
  N2: M1.D2, LCD1.pin_5
  N3: M1.D4, LCD1.pin4
  N4: M1.RX2, LCD1.pin_7
  N5: M1.TX2, LCD1.pin_6
  N6: M1.D5, LCD1.pin3
  N7: M1.D18, RFID.SCK
  N8: M1.D19, RFID.MISO
  N9: M1.D21, RFID.SDA
  N10: M1.D22, RFID.RST
  N11: M1.D23, RFID.MOSI
  N12: M1.EN, C1.+
  N13: M1.VN, T1.Vout
  N14: M1.D32, Relay_BC548_32.signal
  N15: M1.D14, GY1.pin4, M3.SDA
  N16: M1.D12, Relay_BC548_12.signal
  N17: M1.VIN, T1.+Vs, U1.IN+, Relay_BC548_12.power, Relay_BC548_12.ground, Relay_BC548_32.power, Relay_BC548_32.ground
  N18: SIM800L_BO1.PIN2, U1.OUT+
  N19: M2.pin1, Solar_Panel.-
  N20: M2.pin3, BAT1.-
  N21: M2.pin4, BAT1.+
  N22: M2.pin5, U3.IN
  N23: M2.pin6, Solar_Panel.+

custom parts:
  DOIT Esp32 DevKit v1 (30 pins long, 11 pins width): The DOIT Esp32 DevKit v1 is one of the development board created by DOIT to evaluate the ESP-WROOM-32 module. It is based on the ESP32 microcontroller that boasts Wifi, Bluetooth, Ethernet and Low Power support all in a single chip. (vanepp) made breadboard work, adjusted pin numbering and labels and reduced size of schematic and cleaned up pcb. This chip is 30pins long (2 x15) and 11 pins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
  TFT 1.8 inch 160x128 w SD: This is a generic 1.8 tft spi lcd display available on ebay and others. The 1.8" display has 128x160 color pixels.
  LM2596 step down module: LM2596 DC-DC step down power supply module 3 A.
  RFID-RC522-v2: A simple China made RFID-RC522 Reader; do check the pin labels, as this is a MFRC522 based clone.
  TP4056 Module: TP4056 Lithium Battery Charge Management Module Links: TP4056 website
  MPC1700: Small package LDO
  Keyes Relay: The Keyes 5V relay module is suitable for SCM development, home appliance control. It uses a 5V~12V TIL control signal which can control DC / AC signal.
  MPU-6050 Board GY-521: Acelerometro y Giroscopio MPU-6050 Board GY-521
  BME280: Temperature Humidity Barometric presure Sensor
